# Fritzing sketch buttoncamera (saved by Fritzing 0.9.3b)
breadboards: 1

parts:
  Raspberry_Pi_1 = Raspberry Pi 3 [part_number=RPI-3-V1.2]
  IC1 = Rasberry Pi NIOR Camera [chip_label=IC package="DIP (Dual Inline) [THT]"]  # not connected
  S1 = Pushbutton [package="[SMD]"]

nets:
  N1: Raspberry_Pi_1.GPIO2, S1.Pin_1, S1.Pin_2
  N2: Raspberry_Pi_1.GND, S1.Pin_3, S1.Pin_4

custom parts:
  Rasberry Pi NIOR Camera: Camera
