# Fritzing sketch buttonrgbled (saved by Fritzing 0.9.3b)
breadboards: 1

parts:
  Raspberry_Pi_1 = Raspberry Pi 3 [part_number=RPI-3-V1.2]
  IC1 = Rasberry Pi NIOR Camera [chip_label=IC package="DIP (Dual Inline) [THT]"]  # not connected
  S1 = Pushbutton [package="[SMD]"]
  LED1 = RGB LED (com. cathode, rbg) [package="5 mm [THT]"]

nets:
  N1: Raspberry_Pi_1.GPIO2, S1.Pin_1, S1.Pin_2
  N2: Raspberry_Pi_1.GPIO21, LED1.green_anode
  N3: Raspberry_Pi_1.GPIO20, LED1.blue_anode
  N4: Raspberry_Pi_1.GPIO16, LED1.red_anode
  N5: Raspberry_Pi_1.GND, S1.Pin_3, S1.Pin_4, LED1.common_cathode

custom parts:
  Rasberry Pi NIOR Camera: Camera
