# Fritzing sketch distanceledbuzzer (saved by Fritzing 0.9.3b)
breadboards: 1

parts:
  Raspberry_Pi_1 = Raspberry Pi 3 [part_number=RPI-3-V1.2]
  hc-sr1 = hc-sr04
  R1 = Resistor [tolerance=±5% resistance=220 package="2512 [SMD]"]
  R2 = Resistor [tolerance=±5% resistance=220 package="2512 [SMD]"]
  LED1 = smd LED [color="Red (633nm)" package="0805 [SMD]"]
  R3 = Resistor [tolerance=±5% resistance=220 package="2512 [SMD]"]
  J1 = Piezo Speaker

nets:
  N1: Raspberry_Pi_1.GPIO4, hc-sr1.Trig
  N2: Raspberry_Pi_1.GPIO17, R1.Pin_1, R2.Pin_0
  GND: Raspberry_Pi_1.GND, hc-sr1.GND, R2.Pin_1, LED1.cathode, R3.Pin_0, J1.pin1
  N3: Raspberry_Pi_1.GPIO21, J1.pin2
  5V: Raspberry_Pi_1.5V, hc-sr1.VCC
  N4: hc-sr1.Echo, R1.Pin_0
  N5: LED1.anode, R3.Pin_1
