# Fritzing sketch firealarm (saved by Fritzing 0.9.3b)
breadboards: 2

parts:
  U1 = LCD-16X2 [package=lcd-16x2]
  Raspberry_Pi_1 = Raspberry Pi 3 [part_number=RPI-3-V1.2]
  R1 = Rotary Potentiometer (Large) [maximum_resistance=100kΩ package=THT]
  S1 = Momentary Switch [package=ksa_sealed_tac_switch]
  S2 = KY-026
  J1 = Piezo Speaker
  LED1 = RGB LED (com. cathode, rbg) [package="5 mm [THT]"]

nets:
  VSS: U1.VSS, U1.R_W, U1.K, Raspberry_Pi_1.GND, R1.leg1, S1.3, S2.pin2, S2.pin3, S2.pin4, J1.pin2, LED1.common_cathode
  VDD: U1.VDD, U1.A, Raspberry_Pi_1.5V, R1.leg2
  N1: U1.VO, R1.wiper
  N2: U1.RS, Raspberry_Pi_1.GPIO26
  N3: U1.E, Raspberry_Pi_1.GPIO19
  N4: U1.DB4, Raspberry_Pi_1.GPIO25
  N5: U1.DB5, Raspberry_Pi_1.GPIO24
  N6: U1.DB6, Raspberry_Pi_1.GPIO22
  N7: U1.DB7, Raspberry_Pi_1.GPIO27
  N8: Raspberry_Pi_1.3v3, S2.pin1
  N9: Raspberry_Pi_1.GPIO13, J1.pin1
  N10: Raspberry_Pi_1.GPIO21, LED1.red_anode
  N11: Raspberry_Pi_1.GPIO20, LED1.green_anode
  N12: Raspberry_Pi_1.GPIO16, LED1.blue_anode

custom parts:
  KY-026: ky-026 flame sensor module
