# Fritzing sketch flame (saved by Fritzing 0.9.3b)
breadboards: 1

parts:
  Raspberry_Pi_1 = Raspberry Pi 3 [part_number=RPI-3-V1.2]
  S1 = KY-026

nets:
  N1: Raspberry_Pi_1.3v3, S1.pin3
  N2: Raspberry_Pi_1.GPIO3, S1.pin2
  N3: Raspberry_Pi_1.GPIO16, S1.pin4

custom parts:
  KY-026: ky-026 flame sensor module
