# Fritzing sketch flamealarm (saved by Fritzing 0.9.3b)
breadboards: 1

parts:
  Raspberry_Pi_1 = Raspberry Pi 3 [part_number=RPI-3-V1.2]
  S1 = KY-026
  LED1 = smd LED [color="Red (633nm)" package="0805 [SMD]"]
  R1 = Resistor [tolerance=±5% resistance=220 package="2512 [SMD]"]
  J1 = Piezo Speaker

nets:
  N1: Raspberry_Pi_1.3v3, S1.pin3
  N2: Raspberry_Pi_1.GPIO3, S1.pin2
  N3: Raspberry_Pi_1.GPIO17, R1.Pin_0
  N4: Raspberry_Pi_1.GND, LED1.cathode, J1.pin1
  N5: Raspberry_Pi_1.GPIO16, S1.pin4
  N6: Raspberry_Pi_1.GPIO18, J1.pin2
  N7: LED1.anode, R1.Pin_1

custom parts:
  KY-026: ky-026 flame sensor module
