# Fritzing sketch lcdtemp (saved by Fritzing 0.9.3b)
breadboards: 2

parts:
  U1 = LCD-16X2 [package=lcd-16x2]
  Raspberry_Pi_1 = Raspberry Pi 3 [part_number=RPI-3-V1.2]
  R1 = Rotary Potentiometer (Large) [maximum_resistance=100kΩ package=THT]
  Part1 = KY-015 Temperature & Humidity Sensor Module [package="Breakout board"]

nets:
  VSS: U1.VSS, U1.R_W, U1.K, Raspberry_Pi_1.GND, R1.leg1, Part1.-
  VDD: U1.VDD, U1.A, Raspberry_Pi_1.5V, R1.leg2
  N1: U1.VO, R1.wiper
  N2: U1.RS, Raspberry_Pi_1.GPIO26
  N3: U1.E, Raspberry_Pi_1.GPIO19
  N4: U1.DB4, Raspberry_Pi_1.GPIO25
  N5: U1.DB5, Raspberry_Pi_1.GPIO24
  N6: U1.DB6, Raspberry_Pi_1.GPIO22
  N7: U1.DB7, Raspberry_Pi_1.GPIO27
  3V3: Raspberry_Pi_1.3V3, Part1.Vin
  N8: Raspberry_Pi_1.GPIO12, Part1.S

custom parts:
  KY-015 Temperature & Humidity Sensor Module: KY-015 temperature and humidity sensor module, provides a low-latency serial interface to measure humidity and temperature.
