# Fritzing sketch led (saved by Fritzing 0.9.3b)
breadboards: 1

parts:
  Raspberry_Pi_1 = Raspberry Pi 3 [part_number=RPI-3-V1.2]
  LED1 = smd LED [color="White (6500K)" package="1206 [SMD]"]
  R1 = Resistor [tolerance=±5% resistance=220 package="0805 [SMD]"]

nets:
  N1: Raspberry_Pi_1.GIPO17, R1.Pin_0
  N2: Raspberry_Pi_1.GND, LED1.cathode
  N3: LED1.anode, R1.Pin_1
