# Fritzing sketch noise (saved by Fritzing 0.9.3b)

parts:
  Raspberry_Pi_1 = Raspberry Pi 3 [part_number=RPI-3-V1.2]
  부품1 = Breakout Board for Electret Microphone

nets:
  3V3: Raspberry_Pi_1.3v3, 부품1.VCC
  N1: Raspberry_Pi_1.GIPO4, 부품1.AUD
  GND: Raspberry_Pi_1.GND, 부품1.GND
