# Fritzing sketch noiselcd (saved by Fritzing 0.9.3b)
breadboards: 2

parts:
  U1 = LCD-16X2 [package=lcd-16x2]
  Raspberry_Pi_1 = Raspberry Pi 3 [part_number=RPI-3-V1.2]
  R1 = Rotary Potentiometer (Large) [maximum_resistance=100kΩ package=THT]
  LED1 = RGB LED (com. cathode, rgb) [package="5 mm [THT]"]
  부품1 = Breakout Board for Electret Microphone

nets:
  GND: U1.VSS, U1.R_W, U1.K, Raspberry_Pi_1.GND, Raspberry_Pi_1.GPIO20, R1.leg1, LED1.green_anode, 부품1.GND
  VDD: U1.VDD, U1.A, Raspberry_Pi_1.5V, R1.leg2
  N1: U1.VO, R1.wiper
  N2: U1.RS, Raspberry_Pi_1.GPIO26
  N3: U1.E, Raspberry_Pi_1.GPIO19
  N4: U1.DB4, Raspberry_Pi_1.GPIO25
  N5: U1.DB5, Raspberry_Pi_1.GPIO24
  N6: U1.DB6, Raspberry_Pi_1.GPIO22
  N7: U1.DB7, Raspberry_Pi_1.GPIO27
  3V3: Raspberry_Pi_1.3v3, 부품1.VCC
  N8: Raspberry_Pi_1.GPIO17, 부품1.AUD
  N9: Raspberry_Pi_1.GPIO21, LED1.red_anode
  N10: Raspberry_Pi_1.GPIO16, LED1.blue_anode
