# Fritzing sketch noiseled (saved by Fritzing 0.9.3b)
breadboards: 1

parts:
  Raspberry_Pi_1 = Raspberry Pi 3 [part_number=RPI-3-V1.2]
  부품1 = Breakout Board for Electret Microphone
  LED1 = RGB LED (com. cathode, rbg) [package="5 mm [THT]"]

nets:
  3V3: Raspberry_Pi_1.3v3, 부품1.VCC
  N1: Raspberry_Pi_1.GIPO4, 부품1.AUD
  GND: Raspberry_Pi_1.GND, 부품1.GND, LED1.green_anode
  N2: Raspberry_Pi_1.GIPO21, LED1.red_anode
  N3: Raspberry_Pi_1.GIPO20, LED1.common_cathode
  N4: Raspberry_Pi_1.GIPO16, LED1.blue_anode
