# Fritzing sketch photoresistorstreet1 (saved by Fritzing 0.9.3b)
breadboards: 1

parts:
  Raspberry_Pi_1 = Raspberry Pi 3 [part_number=RPI-3-V1.2]
  LED1 = LED - 3mm [color="Yellow (595nm)" package="3 mm [THT]"]
  R1 = Resistor [tolerance=±5% resistance=220 package="1206 [SMD]"]
  Mod1 = KY-018 Photoresistor Module [package="Breakout board"]

nets:
  3V3: Raspberry_Pi_1.3v3, Mod1.Vin
  N1: Raspberry_Pi_1.GIPO17, Mod1.S
  N2: Raspberry_Pi_1.GND, R1.Pin_0, Mod1.-
  N3: Raspberry_Pi_1.GIPO16, LED1.cathode
  N4: LED1.anode, R1.Pin_1

custom parts:
  KY-018 Photoresistor Module: KY-018 Photoresistor module, used to measure light intensity. It can determine the presence or absence of light.
