# Fritzing sketch photoresistorstreet2 (saved by Fritzing 0.9.3b)
breadboards: 1

parts:
  Raspberry_Pi_1 = Raspberry Pi 3 [part_number=RPI-3-V1.2]
  Mod1 = KY-018 Photoresistor Module [package="Breakout board"]
  LED1 = RGB LED (com. cathode, rgb) [package="5 mm [THT]"]

nets:
  3V3: Raspberry_Pi_1.3v3, Mod1.Vin
  N1: Raspberry_Pi_1.GIPO17, Mod1.S
  N2: Raspberry_Pi_1.GND, Mod1.-, LED1.common_cathode
  N3: Raspberry_Pi_1.GIPO21, LED1.blue_anode
  N4: Raspberry_Pi_1.GIPO20, LED1.green_anode
  N5: Raspberry_Pi_1.GIPO16, LED1.red_anode

custom parts:
  KY-018 Photoresistor Module: KY-018 Photoresistor module, used to measure light intensity. It can determine the presence or absence of light.
