# Fritzing sketch rfid (saved by Fritzing 0.9.3b)
breadboards: 1

parts:
  U1 = RFID RC522 SIP - 8 pins [chip_label="RFID RC522" package="SIP (Single Inline) [THT]"]
  Raspberry_Pi_1 = Raspberry Pi 3 [part_number=RPI-3-V1.2]

nets:
  N1: U1.NSS, Raspberry_Pi_1.GPIO8
  N2: U1.SCK, Raspberry_Pi_1.GPIO11
  N3: U1.MOSI, Raspberry_Pi_1.GPIO10
  N4: U1.MISO, Raspberry_Pi_1.GPIO9
  GND: U1.GND, Raspberry_Pi_1.GND
  N5: U1.RST, Raspberry_Pi_1.GPIO25
  VCC: U1.VCC, Raspberry_Pi_1.3v3

custom parts:
  RFID RC522 SIP - 8 pins: A SIP stand-in part for RFID RC522 . With 8 pins on a 300 mil single inline package (SIP) footprint.
