# Fritzing sketch rfidlcd (saved by Fritzing 0.9.3b)
breadboards: 1

parts:
  U1 = LCD-16X2 [package=lcd-16x2]
  Raspberry_Pi_1 = Raspberry Pi 3 [part_number=RPI-3-V1.2]
  R1 = Rotary Potentiometer (Large) [maximum_resistance=100kΩ package=THT]
  U2 = RFID RC522 SIP - 8 pins [chip_label="RFID RC522" package="SIP (Single Inline) [THT]"]

nets:
  GND: U1.VSS, U1.R_W, U1.K, Raspberry_Pi_1.GND, R1.leg1, U2.GND
  VDD: U1.VDD, U1.A, Raspberry_Pi_1.5V, R1.leg2
  N1: U1.VO, R1.wiper
  N2: U1.RS, Raspberry_Pi_1.GPIO26
  N3: U1.E, Raspberry_Pi_1.GPIO19
  N4: U1.DB4, Raspberry_Pi_1.GPIO21
  N5: U1.DB5, Raspberry_Pi_1.GPIO20
  N6: U1.DB6, Raspberry_Pi_1.GPIO16
  N7: U1.DB7, Raspberry_Pi_1.GPIO12
  3V3: Raspberry_Pi_1.3v3, U2.VCC
  N8: Raspberry_Pi_1.GPIO10, U2.MOSI
  N9: Raspberry_Pi_1.GPIO9, U2.MISO
  N10: Raspberry_Pi_1.GPIO11, U2.SCK
  N11: Raspberry_Pi_1.GPIO25, U2.RST
  N12: Raspberry_Pi_1.GPIO18, U2.NSS

custom parts:
  RFID RC522 SIP - 8 pins: A SIP stand-in part for RFID RC522 . With 8 pins on a 300 mil single inline package (SIP) footprint.
