# Fritzing sketch rgbled (saved by Fritzing 0.9.3b)
breadboards: 1

parts:
  Raspberry_Pi_1 = Raspberry Pi 3 [part_number=RPI-3-V1.2]
  LED2 = RGB LED - (4 legs) [package="5 mm [THT]"]

nets:
  N1: Raspberry_Pi_1.GIPO10, LED2.green_cathode
  N2: Raspberry_Pi_1.GIPO9, LED2.red_cathode
  N3: Raspberry_Pi_1.GIPO11, LED2.blue_cathode
  N4: Raspberry_Pi_1.GND, LED2.common_anode
