# Fritzing sketch temphumid (saved by Fritzing 0.9.3b)
breadboards: 1

parts:
  Raspberry_Pi_1 = Raspberry Pi 3 [part_number=RPI-3-V1.2]
  Part1 = KY-015 Temperature & Humidity Sensor Module [package="Breakout board"]

nets:
  3V3: Raspberry_Pi_1.3v3, Part1.Vin
  N1: Raspberry_Pi_1.GPIO12, Part1.S
  N2: Raspberry_Pi_1.GND, Part1.-

custom parts:
  KY-015 Temperature & Humidity Sensor Module: KY-015 temperature and humidity sensor module, provides a low-latency serial interface to measure humidity and temperature.
